# Fritzing sketch DHT22_raspberrry (saved by Fritzing 0.9.10b)

parts:
  Part1 = DHT22 Breakout module [package="Breakout board"]
  Mod1 = Raspberry Pi 4B

nets:
  N1: Part1.Out, Mod1.GPIO18
  N2: Part1.+, Mod1.3V3
  N3: Part1.-, Mod1.GND

custom parts:
  DHT22 Breakout module: DHT22 temperature and humidity sensor module, provides a low-latency serial interface to measure humidity and temperature.
