# Fritzing sketch RaspiCar (saved by Fritzing 0.9.4)

parts:
  Componente1 = Adafruit DC+Stepper Motor HAT [part_number="Adafruit #2348"]
  M1 = DC Motor
  M2 = DC Motor
  M3 = DC Motor
  M4 = DC Motor
  BATT2 = 3xAAA Switchable Battery Pack w/Bare Wire
  HC-SR04_Sensor_1 = HC-SR04 Ultrasonic Distance Sensor
  Componente2 = NeoPixel Stick [part_number=1426]
  BMP280_Breakout1 = BMP280 Breakout Board [part_number=BMP280]
  HC-SR04_Sensor_2 = HC-SR04 Ultrasonic Distance Sensor

nets:
  N1: Componente1.SDA, BMP280_Breakout1.SDA
  N2: Componente1.SCL, BMP280_Breakout1.SCL
  N3: Componente1.GPIO4, HC-SR04_Sensor_1.TRIG
  N4: Componente1.GPIO17, HC-SR04_Sensor_1.ECHO
  GND: Componente1.GPIO18, Componente1.GND, BATT2.NEG, HC-SR04_Sensor_1.GND, Componente2.GND, BMP280_Breakout1.GND, HC-SR04_Sensor_2.GND
  N5: Componente1.GPIO5, HC-SR04_Sensor_2.TRIG
  N6: Componente1.GPIO6, HC-SR04_Sensor_2.ECHO
  N7: Componente1.M2A, M2.pin_1
  N8: Componente1.M2B, M2.pin_2
  N9: Componente1.M1B, M1.pin_1
  N10: Componente1.M1A, M1.pin_2
  N11: Componente1.M4A, M3.pin_1
  N12: Componente1.M4B, M3.pin_2
  N13: Componente1.M3B, M4.pin_1
  N14: Componente1.M3A, M4.pin_2
  N15: Componente1.VMOTOR, BATT2.POS
  VCC: Componente1.5.0V, HC-SR04_Sensor_1.VCC, Componente2.+5V, BMP280_Breakout1.VCC, HC-SR04_Sensor_2.VCC

notes:
  8xNeopixels-GPIO18
  BME280
  I2C
  Ultrasonido 1
  Trig - 4
  Echo - 17
  Ultasonido 2
  Trig - 5
  Echo - 6

custom parts:
  Adafruit DC+Stepper Motor HAT: Let your robotic dreams come true with the new DC+Stepper Motor HAT from Adafruit. This Raspberry Pi add-on is perfect for any motion project as it can drive up to 4 DC or 2 Stepper motors with full PWM speed control. Since the Raspberry Pi does not have a lot of PWM pins, we use a fully-dedicated PWM driver chip onboard to both control motor direction and speed. This chip handles all the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
  3xAAA Switchable Battery Pack w/Bare Wire: 3xAAA Switchable Battery Pack w/Bare Wire Connectors
  NeoPixel Stick: Make your own little LED strip arrangement with this stick of NeoPixel LEDs. We crammed 8 of the tiny 5050 (5mm x 5mm) smart RGB LEDs onto a PCB with mounting holes and a chainable design. Use only one microcontroller pin to control as many as you can chain together! Each LED is addressable as the driver chip is inside the LED. Each one has ~18mA constant current drive so the color will be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
  BMP280 Breakout Board: This is a breakout board for the Bosch Sensortec BMP280, "an absolute barometric pressure sensor especially designed for mobile applications." The operation range is 300 to 1100 hPa. Supply voltage is 1.2 to 3.6V. Operating temperature range is -40 to +85 °C.
